# Fritzing sketch Schematic (saved by Fritzing 0.8.7b)
breadboards: 1

parts:
  U1 = 7-SEGMENT-DISPLAY-1_-RED [package=7-segment-1_pth]
  U2 = 7-SEGMENT-DISPLAY-1_-RED [package=7-segment-1_pth]
  PIC18F14K50 = PICAXE-20M [package=THT]
  U3 = Voltage Regulator - 5V [package="TO220 [THT]"]
  VCC1 = Battery block 9V
  C1 = Ceramic Capacitor [capacitance=100nF package="100 mil [THT, multilayer]"]
  C2 = Electrolytic Capacitor [capacitance=22µF package="100 mil [THT, electrolytic]"]
  U4 = 74HC595 [package="DIP16 [THT]"]
  U5 = 74HC595 [package="DIP16 [THT]"]
  TC74A0 = Header 5 [package=1x05-1mm-ra]
  R1 = Resistor [tolerance=±5% resistance=4.7k package=THT]
  R2 = Resistor [tolerance=±5% resistance=4.7k package=THT]
  C3 = Ceramic Capacitor [capacitance=1nF package="100 mil [THT, multilayer]"]

nets:
  N1: U1.E, U4.Q3
  N2: U1.D, U4.Q4
  GND: U1.G1, U1.G2, U2.G1, U2.G2, PIC18F14K50.0V, U3.GND, VCC1.-, C1.0, C2.-, U4.GND, U4.OE, U5.GND, U5.OE, TC74A0.3, C3.0
  N3: U1.C, U4.Q5
  N4: U1.B, U4.Q6
  N5: U1.A, U4.Q7
  N6: U1.F, U4.Q2
  N7: U1.G, U4.Q1
  N8: U2.E, U5.Q3
  N9: U2.D, U5.Q4
  N10: U2.C, U5.Q5
  N11: U2.B, U5.Q6
  N12: U2.A, U5.Q7
  N13: U2.F, U5.Q2
  N14: U2.G, U5.Q1
  VCC: PIC18F14K50.+V, U3.output_voltage, C2.+, U4.VCC, U5.VCC, TC74A0.5, R1.Pin_1, R2.Pin_1, C3.1
  N15: PIC18F14K50.In_5, U4.DS
  N16: PIC18F14K50.In_4, U5.DS
  N17: PIC18F14K50.In_3_/_ADC_3, U4.ST_CP
  N18: PIC18F14K50.In_2_/_ADC_2, U5.ST_CP
  N19: PIC18F14K50.Out_7, TC74A0.4, R2.Pin_0
  N20: PIC18F14K50.Out_5, TC74A0.2, R1.Pin_0
  N21: PIC18F14K50.Out_4, U4.MR, U5.MR
  N22: PIC18F14K50.Out_3, U5.SH_CP
  N23: PIC18F14K50.Out_2, U4.SH_CP
  N24: U3.input_voltage, VCC1.+, C1.1
